// Logisim project CPU_t3.circ as structural Verilog: 7 circuits, main circuit main
module main (
  input  in_1,
  input  in_2,
  input  in_3,
  input  [4:0] in_4,
  input  [4:0] in_5,
  input  [3:0] in_6,
  output [31:0] out_7
);

  wire adr_clear, adr_color, adr_kmt, adr_posx, adr_posy, and_1_out, and_2_out, and_3_out, and_4_out,
       and_5_out, and_6_out, and_7_out, and_8_out, and_9_out, and_10_out, and_11_out, and_12_out, and_13_out,
       CLK, comparator_1_eq, comparator_2_lt, comparator_8_eq, comparator_9_eq, comparator_10_eq,
       comparator_11_eq, comparator_12_eq, comparator_13_eq, comparator_14_gt, comparator_15_eq,
       comparator_16_lt, comparator_17_eq, comparator_18_gt, comparator_19_lt, comparator_20_eq,
       comparator_21_eq, comparator_22_eq, comparator_23_eq, comparator_24_eq, CPU_read, CPU_write,
       deb_intFlags, deb_intMask, deb_isr, Keyboard_INT, Keyboard_out, or_1_out, or_2_out, or_3_out,
       or_4_out, por_1_out, register_6_q, resetCPU;
  wire [2:0] Flag_Reg, Posta_A, Posta_B;
  wire [3:0] bit_extender_2_out, bit_extender_2_out_2, bit_extender_3_out, bit_extender_3_out_2,
       rgb_video_1_p6;
  wire [4:0] rgb_video_1_p4, rgb_video_1_p5;
  wire [6:0] bitselector_1_out, controlled_buffer_4_out, keyboard_1_data;
  wire [20:0] bitselector_2_out, register_7_q;
  wire [23:0] controlled_buffer_1_out, cpu_1_outaddress;
  wire [31:0] bit_extender_1_out, controlled_buffer_2_out, cpu_1_outdata, deb_adr, deb_r0, deb_r1, deb_r2,
       deb_r3, deb_r4, deb_r5, deb_r6, deb_stackReg, IR, MAR, MDR, PC, ram_1_dout;
  wire [31:24] cpu_1_outaddress_2;
  wire [34:0] Command;

  Comparator #(.width(32)) comparator_1 (.a(MAR), .b({32{1'b0}}), .eq(comparator_1_eq));  // open: gt, lt
  and and_1 (and_1_out, CPU_write, comparator_1_eq);
  CPU cpu_1 (
    .CLK(CLK), .inData(out_7), .interrupt_in(Keyboard_INT), .resetCPU(resetCPU),
    .outAddress({cpu_1_outaddress_2, cpu_1_outaddress}), .outData(cpu_1_outdata), .Read(CPU_read),
    .Write(CPU_write), .deb_PC(PC), .deb_MAR(MAR), .deb_IR(IR), .deb_MDR(MDR), .debFlagReg(Flag_Reg),
    .deb_posta_A(Posta_A), .deb_posta_B(Posta_B), .deb_stackReg(deb_stackReg), .deb_r6(deb_r6),
    .deb_r5(deb_r5), .deb_r4(deb_r4), .deb_r3(deb_r3), .deb_r2(deb_r2), .deb_r1(deb_r1), .deb_r0(deb_r0),
    .deb_intFlags(deb_intFlags), .deb_AdrReg(deb_adr), .deb_isr(deb_isr), .deb_intMask(deb_intMask),
    .command(Command));
  Register #(.width(32)) register_1 (.D(IR), .en(and_1_out), .clk(and_1_out));  // open: Q, clr
  Comparator #(.mode("unsigned"), .width(32)) comparator_2 (
    .a({cpu_1_outaddress_2, cpu_1_outaddress}), .b(32'hfffffff6), .eq(adr_clear), .lt(comparator_2_lt));  // open: gt
  Comparator #(.mode("unsigned"), .width(32)) comparator_3 (
    .a({cpu_1_outaddress_2, cpu_1_outaddress}), .b(32'hfffffff7), .eq(Keyboard_out));  // open: gt, lt
  Comparator #(.mode("unsigned"), .width(32)) comparator_4 (
    .a({cpu_1_outaddress_2, cpu_1_outaddress}), .b(32'hfffffff8), .eq(adr_posy));  // open: gt, lt
  Comparator #(.mode("unsigned"), .width(32)) comparator_5 (
    .a({cpu_1_outaddress_2, cpu_1_outaddress}), .b(32'hfffffff9), .eq(adr_posx));  // open: gt, lt
  Comparator #(.mode("unsigned"), .width(32)) comparator_6 (
    .a({cpu_1_outaddress_2, cpu_1_outaddress}), .b(32'hfffffffa), .eq(adr_color));  // open: gt, lt
  Comparator #(.mode("unsigned"), .width(32)) comparator_7 (
    .a({cpu_1_outaddress_2, cpu_1_outaddress}), .b(32'hfffffffb), .eq(adr_kmt));  // open: gt, lt
  Comparator #(.mode("unsigned"), .width(32)) comparator_8 (
    .a({cpu_1_outaddress_2, cpu_1_outaddress}), .b(32'hfffffffc), .eq(comparator_8_eq));  // open: gt, lt
  Comparator #(.mode("unsigned"), .width(32)) comparator_9 (
    .a({cpu_1_outaddress_2, cpu_1_outaddress}), .b(32'hfffffffd), .eq(comparator_9_eq));  // open: gt, lt
  Comparator #(.mode("unsigned"), .width(32)) comparator_10 (
    .a({cpu_1_outaddress_2, cpu_1_outaddress}), .b(32'hfffffffe), .eq(comparator_10_eq));  // open: gt, lt
  Comparator #(.mode("unsigned"), .width(32)) comparator_11 (
    .a({cpu_1_outaddress_2, cpu_1_outaddress}), .b({32{1'b1}}), .eq(comparator_11_eq));  // open: gt, lt
  Hex_Digit_Display hex_digit_display_1 (.value(deb_stackReg[31:28]));  // open: dp
  Hex_Digit_Display hex_digit_display_2 (.value(PC[31:28]));  // open: dp
  Hex_Digit_Display hex_digit_display_3 (.value(MDR[31:28]));  // open: dp
  Hex_Digit_Display hex_digit_display_4 (.value(IR[31:28]));  // open: dp
  Hex_Digit_Display hex_digit_display_5 (.value({1'b0, Command[34:32]}));  // open: dp
  Hex_Digit_Display hex_digit_display_6 (.value(Command[31:28]));  // open: dp
  Hex_Digit_Display hex_digit_display_7 (.value(deb_stackReg[27:24]));  // open: dp
  Hex_Digit_Display hex_digit_display_8 (.value(deb_stackReg[23:20]));  // open: dp
  Hex_Digit_Display hex_digit_display_9 (.value(deb_r6[31:28]));  // open: dp
  Hex_Digit_Display hex_digit_display_10 (.value(deb_r5[31:28]));  // open: dp
  Hex_Digit_Display hex_digit_display_11 (.value(deb_r4[31:28]));  // open: dp
  assign controlled_buffer_1_out = comparator_2_lt ? cpu_1_outaddress : 24'bz;  // Controlled_Buffer controlled_buffer_1
  Hex_Digit_Display hex_digit_display_12 (.value(PC[27:24]));  // open: dp
  Hex_Digit_Display hex_digit_display_13 (.value(PC[23:20]));  // open: dp
  Hex_Digit_Display hex_digit_display_14 (.value(MDR[27:24]));  // open: dp
  Hex_Digit_Display hex_digit_display_15 (.value(MDR[23:20]));  // open: dp
  Hex_Digit_Display hex_digit_display_16 (.value(IR[27:24]));  // open: dp
  Hex_Digit_Display hex_digit_display_17 (.value(IR[23:20]));  // open: dp
  Hex_Digit_Display hex_digit_display_18 (.value(Command[27:24]));  // open: dp
  Hex_Digit_Display hex_digit_display_19 (.value(Command[23:20]));  // open: dp
  Hex_Digit_Display hex_digit_display_20 (.value(deb_stackReg[19:16]));  // open: dp
  Hex_Digit_Display hex_digit_display_21 (.value(deb_stackReg[15:12]));  // open: dp
  Hex_Digit_Display hex_digit_display_22 (.value(deb_r6[27:24]));  // open: dp
  Hex_Digit_Display hex_digit_display_23 (.value(deb_r6[23:20]));  // open: dp
  Hex_Digit_Display hex_digit_display_24 (.value(deb_r5[27:24]));  // open: dp
  Hex_Digit_Display hex_digit_display_25 (.value(deb_r5[23:20]));  // open: dp
  Hex_Digit_Display hex_digit_display_26 (.value(deb_r4[27:24]));  // open: dp
  Hex_Digit_Display hex_digit_display_27 (.value(deb_r4[23:20]));  // open: dp
  and and_2 (and_2_out, comparator_2_lt, CPU_write);
  Hex_Digit_Display hex_digit_display_28 (.value(PC[15:12]));  // open: dp
  Hex_Digit_Display hex_digit_display_29 (.value(PC[19:16]));  // open: dp
  Hex_Digit_Display hex_digit_display_30 (.value(MDR[15:12]));  // open: dp
  Hex_Digit_Display hex_digit_display_31 (.value(MDR[19:16]));  // open: dp
  Hex_Digit_Display hex_digit_display_32 (.value(IR[15:12]));  // open: dp
  Hex_Digit_Display hex_digit_display_33 (.value(IR[19:16]));  // open: dp
  Hex_Digit_Display hex_digit_display_34 (.value(Command[15:12]));  // open: dp
  Hex_Digit_Display hex_digit_display_35 (.value(Command[19:16]));  // open: dp
  Hex_Digit_Display hex_digit_display_36 (.value(deb_stackReg[7:4]));  // open: dp
  Hex_Digit_Display hex_digit_display_37 (.value(deb_stackReg[11:8]));  // open: dp
  Hex_Digit_Display hex_digit_display_38 (.value(deb_r6[15:12]));  // open: dp
  Hex_Digit_Display hex_digit_display_39 (.value(deb_r6[19:16]));  // open: dp
  Hex_Digit_Display hex_digit_display_40 (.value(deb_r5[15:12]));  // open: dp
  Hex_Digit_Display hex_digit_display_41 (.value(deb_r5[19:16]));  // open: dp
  Hex_Digit_Display hex_digit_display_42 (.value(deb_r4[15:12]));  // open: dp
  Hex_Digit_Display hex_digit_display_43 (.value(deb_r4[19:16]));  // open: dp
  RAM #(.addrWidth(24), .dataWidth(32), .trigger("falling"), .\type ("nonvolatile")) ram_1 (
    .addr(controlled_buffer_1_out), .we(CPU_write), .oe(CPU_read), .clk(CLK), .din(controlled_buffer_2_out),
    .dout(ram_1_dout));
  assign controlled_buffer_2_out = and_2_out ? cpu_1_outdata : 32'bz;  // Controlled_Buffer controlled_buffer_2
  Hex_Digit_Display hex_digit_display_44 (.value(PC[11:8]));  // open: dp
  Hex_Digit_Display hex_digit_display_45 (.value(PC[7:4]));  // open: dp
  Hex_Digit_Display hex_digit_display_46 (.value(MDR[11:8]));  // open: dp
  Hex_Digit_Display hex_digit_display_47 (.value(MDR[7:4]));  // open: dp
  Hex_Digit_Display hex_digit_display_48 (.value(IR[11:8]));  // open: dp
  Hex_Digit_Display hex_digit_display_49 (.value(IR[7:4]));  // open: dp
  Hex_Digit_Display hex_digit_display_50 (.value(Command[11:8]));  // open: dp
  Hex_Digit_Display hex_digit_display_51 (.value(Command[7:4]));  // open: dp
  Hex_Digit_Display hex_digit_display_52 (.value(deb_stackReg[3:0]));  // open: dp
  Hex_Digit_Display hex_digit_display_53 (.value(deb_r6[11:8]));  // open: dp
  Hex_Digit_Display hex_digit_display_54 (.value(deb_r6[7:4]));  // open: dp
  Hex_Digit_Display hex_digit_display_55 (.value(deb_r5[11:8]));  // open: dp
  Hex_Digit_Display hex_digit_display_56 (.value(deb_r5[7:4]));  // open: dp
  Hex_Digit_Display hex_digit_display_57 (.value(deb_r4[11:8]));  // open: dp
  Hex_Digit_Display hex_digit_display_58 (.value(deb_r4[7:4]));  // open: dp
  Hex_Digit_Display hex_digit_display_59 (.value(PC[3:0]));  // open: dp
  Hex_Digit_Display hex_digit_display_60 (.value(MDR[3:0]));  // open: dp
  Hex_Digit_Display hex_digit_display_61 (.value(IR[3:0]));  // open: dp
  Hex_Digit_Display hex_digit_display_62 (.value(Command[3:0]));  // open: dp
  Hex_Digit_Display hex_digit_display_63 (.value(deb_r6[3:0]));  // open: dp
  Hex_Digit_Display hex_digit_display_64 (.value(deb_r5[3:0]));  // open: dp
  Hex_Digit_Display hex_digit_display_65 (.value(deb_r4[3:0]));  // open: dp
  Comparator #(.width(32)) comparator_12 (
    .a(32'ha), .b(controlled_buffer_2_out), .eq(comparator_12_eq));  // open: gt, lt
  Comparator #(.width(24)) comparator_13 (
    .a(controlled_buffer_1_out), .b(24'h8), .eq(comparator_13_eq));  // open: gt, lt
  Hex_Digit_Display hex_digit_display_66 (.value(MAR[31:28]));  // open: dp
  Hex_Digit_Display hex_digit_display_67 (.value(deb_r3[31:28]));  // open: dp
  Hex_Digit_Display hex_digit_display_68 (.value(deb_r2[31:28]));  // open: dp
  Hex_Digit_Display hex_digit_display_69 (.value(deb_r1[31:28]));  // open: dp
  Hex_Digit_Display hex_digit_display_70 (.value(deb_r0[31:28]));  // open: dp
  and and_3 (and_3_out, comparator_2_lt, CPU_read);
  Comparator #(.width(32)) comparator_14 (.a(MAR), .b(32'h8), .gt(comparator_14_gt));  // open: eq, lt
  Comparator #(.width(32)) comparator_15 (.a(MAR), .b(32'h8), .eq(comparator_15_eq));  // open: gt, lt
  Hex_Digit_Display hex_digit_display_71 (.value(MAR[27:24]));  // open: dp
  Hex_Digit_Display hex_digit_display_72 (.value(MAR[23:20]));  // open: dp
  LED led_1 (.in(deb_intFlags));
  LED led_2 (.in(deb_isr));
  LED led_3 (.in(deb_intMask));
  Hex_Digit_Display hex_digit_display_73 (.value({1'b0, Posta_A}));  // open: dp
  Hex_Digit_Display hex_digit_display_74 (.value(deb_r3[27:24]));  // open: dp
  Hex_Digit_Display hex_digit_display_75 (.value(deb_r3[23:20]));  // open: dp
  Hex_Digit_Display hex_digit_display_76 (.value(deb_r2[27:24]));  // open: dp
  Hex_Digit_Display hex_digit_display_77 (.value(deb_r2[23:20]));  // open: dp
  Hex_Digit_Display hex_digit_display_78 (.value(deb_r1[27:24]));  // open: dp
  Hex_Digit_Display hex_digit_display_79 (.value(deb_r1[23:20]));  // open: dp
  Hex_Digit_Display hex_digit_display_80 (.value(deb_r0[27:24]));  // open: dp
  Hex_Digit_Display hex_digit_display_81 (.value(deb_r0[23:20]));  // open: dp
  assign out_7 = and_3_out ? ram_1_dout : 32'bz;  // Controlled_Buffer controlled_buffer_3
  and and_4 (and_4_out, CPU_write, comparator_14_gt);
  Hex_Digit_Display hex_digit_display_82 (.value(MAR[19:16]));  // open: dp
  Hex_Digit_Display hex_digit_display_83 (.value(MAR[15:12]));  // open: dp
  Hex_Digit_Display hex_digit_display_84 (.value(deb_r3[19:16]));  // open: dp
  Hex_Digit_Display hex_digit_display_85 (.value(deb_r3[15:12]));  // open: dp
  Hex_Digit_Display hex_digit_display_86 (.value(deb_r2[19:16]));  // open: dp
  Hex_Digit_Display hex_digit_display_87 (.value(deb_r2[15:12]));  // open: dp
  Hex_Digit_Display hex_digit_display_88 (.value(deb_r1[19:16]));  // open: dp
  Hex_Digit_Display hex_digit_display_89 (.value(deb_r1[15:12]));  // open: dp
  Hex_Digit_Display hex_digit_display_90 (.value(deb_r0[19:16]));  // open: dp
  Hex_Digit_Display hex_digit_display_91 (.value(deb_r0[15:12]));  // open: dp
  Register #(.width(32)) register_2 (.D(IR), .en(comparator_13_eq), .clk(comparator_13_eq));  // open: Q, clr
  Register #(.width(32)) register_3 (.D(IR), .en(comparator_12_eq), .clk(comparator_12_eq));  // open: Q, clr
  Register #(.width(32)) register_4 (.D(MDR), .en(and_4_out), .clk(and_4_out));  // open: Q, clr
  and and_5 (and_5_out, CPU_write, comparator_15_eq);
  Hex_Digit_Display hex_digit_display_92 (.value(MAR[11:8]));  // open: dp
  Hex_Digit_Display hex_digit_display_93 (.value(MAR[7:4]));  // open: dp
  Hex_Digit_Display hex_digit_display_94 (.value({1'b0, Posta_B}));  // open: dp
  Hex_Digit_Display hex_digit_display_95 (.value(deb_r3[11:8]));  // open: dp
  Hex_Digit_Display hex_digit_display_96 (.value(deb_r3[7:4]));  // open: dp
  Hex_Digit_Display hex_digit_display_97 (.value(deb_r2[11:8]));  // open: dp
  Hex_Digit_Display hex_digit_display_98 (.value(deb_r2[7:4]));  // open: dp
  Hex_Digit_Display hex_digit_display_99 (.value(deb_r1[11:8]));  // open: dp
  Hex_Digit_Display hex_digit_display_100 (.value(deb_r1[7:4]));  // open: dp
  Hex_Digit_Display hex_digit_display_101 (.value(deb_r0[11:8]));  // open: dp
  Hex_Digit_Display hex_digit_display_102 (.value(deb_r0[7:4]));  // open: dp
  Register #(.width(32)) register_5 (.D(IR), .en(and_5_out), .clk(and_5_out));  // open: Q, clr
  Hex_Digit_Display hex_digit_display_103 (.value(MAR[3:0]));  // open: dp
  Hex_Digit_Display hex_digit_display_104 (.value(deb_r3[3:0]));  // open: dp
  Hex_Digit_Display hex_digit_display_105 (.value(deb_r2[3:0]));  // open: dp
  Hex_Digit_Display hex_digit_display_106 (.value(deb_r1[3:0]));  // open: dp
  Hex_Digit_Display hex_digit_display_107 (.value(deb_r0[3:0]));  // open: dp
  Hex_Digit_Display hex_digit_display_108 (.value(deb_adr[31:28]));  // open: dp
  BitSelector #(.group(7), .width(32)) bitselector_1 (.in(cpu_1_outdata), .out(bitselector_1_out), .sel(3'b000));
  assign controlled_buffer_4_out = comparator_11_eq ? bitselector_1_out : 7'bz;  // Controlled_Buffer controlled_buffer_4
  Hex_Digit_Display hex_digit_display_109 (.value(deb_adr[27:24]));  // open: dp
  Hex_Digit_Display hex_digit_display_110 (.value(deb_adr[23:20]));  // open: dp
  TTY #(.cols(50), .rows(16)) tty_1 (.data(controlled_buffer_4_out), .clk(CLK), .we(and_6_out), .clr(resetCPU));
  and and_6 (and_6_out, comparator_11_eq, CPU_write);
  Hex_Digit_Display hex_digit_display_111 (.value(deb_adr[19:16]));  // open: dp
  Hex_Digit_Display hex_digit_display_112 (.value(deb_adr[15:12]));  // open: dp
  BitSelector #(.group(21), .width(32)) bitselector_2 (.in(cpu_1_outdata), .out(bitselector_2_out), .sel(1'b0));
  and and_7 (and_7_out, comparator_10_eq, CPU_write);
  Register #(.width(1)) register_6 (.D(comparator_9_eq), .en(CPU_write), .clk(CLK), .Q(register_6_q));  // open: clr
  and and_8 (and_8_out, Keyboard_out, CPU_read);
  Hex_Digit_Display hex_digit_display_113 (.value(deb_adr[11:8]));  // open: dp
  Hex_Digit_Display hex_digit_display_114 (.value(deb_adr[7:4]));  // open: dp
  LED led_4 (.in(Flag_Reg[0]));
  LED led_5 (.in(Flag_Reg[1]));
  LED led_6 (.in(Flag_Reg[2]));
  or or_1 (or_1_out, and_7_out, register_6_q);
  Comparator #(.width(32)) comparator_16 (.a(MAR), .b(32'h31), .lt(comparator_16_lt));  // open: gt, eq
  Comparator #(.width(32)) comparator_17 (.a(MAR), .b({32{1'b0}}), .eq(comparator_17_eq));  // open: gt, lt
  Comparator #(.width(32)) comparator_18 (.a(MAR), .b(32'h20), .gt(comparator_18_gt));  // open: eq, lt
  Comparator #(.width(32)) comparator_19 (.a(MAR), .b(32'h9d), .lt(comparator_19_lt));  // open: gt, eq
  Keyboard #(.buflen(1)) keyboard_1 (
    .clk(CLK), .re(and_8_out), .avail(Keyboard_INT), .data(keyboard_1_data));  // open: clr
  Hex_Digit_Display hex_digit_display_115 (.value(deb_adr[3:0]));  // open: dp
  or or_2 (or_2_out, comparator_16_lt, comparator_17_eq);
  and and_9 (and_9_out, comparator_18_gt, comparator_19_lt);
  Comparator comparator_20 (.a(IR[31:24]), .b(8'h1b), .eq(comparator_20_eq));  // open: gt, lt
  Comparator comparator_21 (.a(IR[31:24]), .b(8'h10), .eq(comparator_21_eq));  // open: gt, lt
  Comparator comparator_22 (.a(IR[31:24]), .b(8'h2), .eq(comparator_22_eq));  // open: gt, lt
  Comparator comparator_23 (.a(IR[31:24]), .b(8'h1), .eq(comparator_23_eq));  // open: gt, lt
  Comparator comparator_24 (.a(IR[31:24]), .b(8'h4), .eq(comparator_24_eq));  // open: gt, lt
  LED OS (.in(or_2_out));
  LED saveSystem (.in(and_9_out));
  // Digital_Oscilloscope digital_oscilloscope_1: pin names not known; wires that end beside it: CLK, CPU_read, Keyboard_out, and_8_out
  LED JMP (.in(comparator_20_eq));
  Register #(.width(21)) register_7 (.D(bitselector_2_out), .en(CPU_write), .clk(CLK), .Q(register_7_q));  // open: clr
  or or_3 (or_3_out, adr_posy, adr_posx, adr_color, adr_kmt);
  LED ADD (.in(comparator_21_eq));
  or or_4 (or_4_out, adr_clear, resetCPU, por_1_out);
  Button reset (.out(resetCPU));
  assign bit_extender_1_out = {{25{1'b0}}, keyboard_1_data};  // Bit_Extender bit_extender_1
  LED sGPU (.in(or_3_out));
  LED STR (.in(comparator_22_eq));
  // Buzzer buzzer_1: pin names not known; wires that end beside it: bitselector_2_out[13:0], bitselector_2_out[20:14], or_1_out, register_7_q[13:0], or_1_out, register_7_q[20:14], CPU_write, comparator_8_eq
  POR #(.PorHighDuration(1)) por_1 (.out(por_1_out));
  assign out_7 = and_8_out ? bit_extender_1_out : 32'bz;  // Controlled_Buffer controlled_buffer_5
  LED LOAD (.in(comparator_23_eq));
  Clock clock_1 (.out(CLK));
  LED RET (.in(comparator_24_eq));
  // RGB_Video #(.cursor("No Cursor"), .height(32), .scale(8), .width(32)) rgb_video_1: pin names not known; wires that end beside it: or_4_out, CLK, 1'b1, rgb_video_1_p4, rgb_video_1_p5, rgb_video_1_p6
  and and_10 (and_10_out, CPU_write, adr_kmt);
  and and_11 (and_11_out, CPU_write, adr_color);
  and and_12 (and_12_out, CPU_write, adr_posx);
  and and_13 (and_13_out, CPU_write, adr_posy);
  GPU gpu_1 (
    .CLK(CLK), .kmt_we(and_10_out), .color_we(and_11_out), .posx_we(and_12_out), .posy_we(and_13_out),
    .Data(cpu_1_outdata), .out_color(rgb_video_1_p6), .deb_posx(rgb_video_1_p4), .deb_posy(rgb_video_1_p5));  // open: deb_kmt
  assign {bit_extender_2_out_2, bit_extender_2_out} = {{3{1'b0}}, rgb_video_1_p4};  // Bit_Extender bit_extender_2
  Hex_Digit_Display hex_digit_display_116 (.value(bit_extender_2_out_2));  // open: dp
  Hex_Digit_Display hex_digit_display_117 (.value(bit_extender_2_out));  // open: dp
  assign {bit_extender_3_out_2, bit_extender_3_out} = {{3{1'b0}}, rgb_video_1_p5};  // Bit_Extender bit_extender_3
  Hex_Digit_Display hex_digit_display_118 (.value(rgb_video_1_p6));  // open: dp
  Hex_Digit_Display hex_digit_display_119 (.value(bit_extender_3_out_2));  // open: dp
  Hex_Digit_Display hex_digit_display_120 (.value(bit_extender_3_out));  // open: dp
  // RGB_Video #(.cursor("No Cursor"), .height(32), .scale(8), .width(32)) rgb_video_2: pin names not known; wires that end beside it: in_1, in_2, in_3, in_4, in_5, in_6

  // Other names for the same wires on the sheet: inData[31:0] = out_7

  // Notes on the sheet:
  //   21: Read; MDR_we
  //   C0: MDR_out; IR_we
  //   8008:  pc_enb, mar_we | pc++; mar = pc;
  //   tty
  //   write
  //   A < B
  //   A == B
  //   A > B
endmodule

module CPU (
  input  CLK,
  input  [31:0] inData,
  input  interrupt_in,
  input  resetCPU,
  output [31:0] outAddress,
  output [31:0] outData,
  output Read,
  output Write,
  output [31:0] deb_PC,
  output [31:0] deb_MAR,
  output [31:0] deb_IR,
  output [31:0] deb_MDR,
  output [2:0] debFlagReg,
  output [2:0] deb_posta_A,
  output [2:0] deb_posta_B,
  output [31:0] deb_stackReg,
  output [31:0] deb_r6,
  output [31:0] deb_r5,
  output [31:0] deb_r4,
  output [31:0] deb_r3,
  output [31:0] deb_r2,
  output [31:0] deb_r1,
  output [31:0] deb_r0,
  output deb_intFlags,
  output [31:0] deb_AdrReg,
  output deb_isr,
  output deb_intMask,
  output [34:0] command
);

  wire and_1_out, and_2_out, and_3_out, and_4_out, controlunit_1_ir_clear, INT_LOAD, INT_MAR, INT_mask_cls,
       int_mask_we, INT_PC_enb, INT_postaMUX, IR_clear, ISR_clear, ISR_we, or_1_out, or_2_out, or_3_out,
       or_4_out, or_6_out;
  wire [2:0] alu_1_cmp_less, multiplexer_1_out, Posta, sp_sel;
  wire [3:0] controlled_buffer_7_out;
  wire [31:0] ACC_q, adder_1_out, alu_1_alu_out, controlled_buffer_2_out, controlled_buffer_8_out,
       controlunit_1_int_jmp_adr, multiplexer_2_out, multiplexer_3_out, multiplexer_4_out, multiplexer_5_out,
       registerfile_1_regout, TEMP_q;

  Multiplexer #(.width(3)) multiplexer_1 (.in0(Posta), .in1(sp_sel), .out(multiplexer_1_out), .sel(INT_postaMUX));
  or or_1 (or_1_out, ISR_clear, resetCPU);
  Register #(.width(32)) MDR (.D(inData), .en(command[5]), .clk(CLK), .Q(deb_MDR), .clr(resetCPU));
  Register #(.width(32)) AddressRegister (
    .D(multiplexer_2_out), .en(command[16]), .clk(CLK), .Q(deb_AdrReg), .clr(resetCPU));
  Multiplexer #(.width(32)) multiplexer_2 (.in0(inData), .in1(adder_1_out), .out(multiplexer_2_out), .sel(command[18]));
  or or_2 (or_2_out, INT_mask_cls, resetCPU);
  assign outData = command[6] ? deb_MDR : 32'bz;  // Controlled_Buffer controlled_buffer_1
  assign controlled_buffer_2_out = command[17] ? deb_AdrReg : 32'bz;  // Controlled_Buffer controlled_buffer_2
  Adder #(.width(32)) adder_1 (.a(deb_AdrReg), .b(outData), .out(adder_1_out));  // open: cin, cout
  Register #(.width(1)) Interrupt_Flags (
    .D(interrupt_in), .en(interrupt_in), .clk(CLK), .Q(deb_intFlags), .clr(or_1_out));
  RegisterFile registerfile_1 (
    .CLK(CLK), .inData(outData), .WE(command[26]), .REG_inSel(multiplexer_1_out),
    .REG_outSel(multiplexer_1_out), .OUT_enb(command[25]), .up_down(command[31]), .sp_enb(command[24]),
    .reset(resetCPU), .deb_reg0(deb_r0), .deb_reg1(deb_r1), .deb_reg2(deb_r2), .deb_reg3(deb_r3),
    .deb_reg4(deb_r4), .deb_reg5(deb_r5), .deb_reg6(deb_r6), .deb_reg7(deb_stackReg),
    .regOut(registerfile_1_regout));
  assign controlled_buffer_2_out = command[29] ? outData : 32'bz;  // Controlled_Buffer controlled_buffer_3
  Register #(.width(1)) ISR (.D(deb_intFlags), .en(ISR_we), .clk(CLK), .Q(deb_isr), .clr(or_1_out));
  assign registerfile_1_regout = command[28] ? outData : 32'bz;  // Controlled_Buffer controlled_buffer_4
  assign outData = command[27] ? registerfile_1_regout : 32'bz;  // Controlled_Buffer controlled_buffer_5
  Register #(.width(32)) TEMP (.D(registerfile_1_regout), .en(command[9]), .clk(CLK), .Q(TEMP_q), .clr(resetCPU));
  assign outData = command[30] ? TEMP_q : 32'bz;  // Controlled_Buffer controlled_buffer_6
  Register #(.width(1)) Interrupt_Mask (.D(int_mask_we), .en(int_mask_we), .clk(CLK), .Q(deb_intMask), .clr(or_2_out));
  Register #(.width(32)) InstructionRegister (.D(outData), .en(command[7]), .clk(CLK), .Q(deb_IR), .clr(IR_clear));
  Multiplexer #(.width(32)) multiplexer_3 (
    .in0(registerfile_1_regout), .in1(outData), .out(multiplexer_3_out), .sel(command[22]));
  assign controlled_buffer_7_out = command[19] ? deb_IR[27:24] : 4'bz;  // Controlled_Buffer controlled_buffer_7
  and and_1 (and_1_out, and_2_out, and_3_out);
  and and_2 (and_2_out, controlled_buffer_7_out[3], ~controlled_buffer_7_out[2]);  // AND_Gate
  and and_3 (and_3_out, ~controlled_buffer_7_out[1], ~controlled_buffer_7_out[0]);  // AND_Gate
  ALU alu_1 (
    .inA(TEMP_q), .inB(multiplexer_3_out), .I3B(controlled_buffer_7_out), .ALU_out(alu_1_alu_out),
    .cmp_greater(alu_1_cmp_less[2]), .cmp_equal(alu_1_cmp_less[1]), .cmp_less(alu_1_cmp_less[0]));
  or or_3 (or_3_out, command[4], INT_LOAD);
  Multiplexer #(.width(32)) multiplexer_4 (
    .in0(controlled_buffer_8_out), .in1(controlunit_1_int_jmp_adr), .out(multiplexer_4_out), .sel(INT_LOAD));
  assign controlled_buffer_8_out = command[4] ? controlled_buffer_2_out : 32'bz;  // Controlled_Buffer controlled_buffer_8
  ControlUnit controlunit_1 (
    .isr_active(deb_isr), .CLK(CLK), .reset(resetCPU), .IR_in(deb_IR), .interrupt(deb_intFlags),
    .int_mask(deb_intMask), .flag_reg(debFlagReg), .sp_sel(sp_sel), .int_postaMUX(INT_postaMUX),
    .int_load(INT_LOAD), .int_pc_enb(INT_PC_enb), .int_mar(INT_MAR), .isr_we(ISR_we),
    .int_mask_cls(INT_mask_cls), .ir_clear(controlunit_1_ir_clear), .int_mask_we(int_mask_we),
    .int_jmp_adr(controlunit_1_int_jmp_adr), .isr_clear(ISR_clear), .controlBits(command), .posta(Posta),
    .deb_posta_A(deb_posta_A), .deb_posta_B(deb_posta_B));
  or or_4 (or_4_out, command[3], INT_PC_enb);
  or or_5 (IR_clear, controlunit_1_ir_clear, resetCPU);
  Register #(.width(32)) ACC (.D(alu_1_alu_out), .en(command[23]), .clk(CLK), .Q(ACC_q), .clr(resetCPU));
  Counter #(.max('hffffffff), .width(32)) ProgramCounter (
    .load(or_3_out), .D(multiplexer_4_out), .count(or_4_out), .Q(deb_PC), .clk(CLK), .clr(resetCPU));  // open: carry, up
  Multiplexer #(.width(32)) multiplexer_5 (
    .in0(deb_PC), .in1(controlled_buffer_2_out), .out(multiplexer_5_out), .sel(command[2]));
  assign outData = command[21] ? ACC_q : 32'bz;  // Controlled_Buffer controlled_buffer_9
  assign outData = command[33] ? deb_PC : 32'bz;  // Controlled_Buffer controlled_buffer_10
  or or_6 (or_6_out, INT_MAR, command[15]);
  Register #(.width(32)) MAR (.D(multiplexer_5_out), .en(or_6_out), .clk(CLK), .Q(deb_MAR), .clr(resetCPU));
  and and_4 (and_4_out, and_1_out, command[19]);
  Register #(.width(3)) FlagRegister (.D(alu_1_cmp_less), .en(and_4_out), .clk(CLK), .Q(debFlagReg));  // open: clr

  assign outAddress = deb_MAR;
  assign Read = command[0];
  assign Write = command[1];

  // Other names for the same wires on the sheet: PC_mux = command[2]; PC_enb = command[3]; PC_load = command[4];
  //   MDR_we = command[5]; MDR_out = command[6]; IR_we = command[7]; IR_out = command[8]; TEMP_we = command[9];
  //   Posta_A_we = command[10]; Posta_A_out = command[11]; Posta_B_we = command[12]; Posta_B_out = command[13];
  //   MAR_load = command[14]; MAR_we = command[15]; ADR_we = command[16]; ADR_out = command[17];
  //   ADR_mux = command[18]; I3B = command[19]; ALU_in = command[20]; ALU_out = command[21]; ALU_mux = command[22];
  //   ACC_we = command[23]; SP_INC = command[24]; REG_out = command[25]; REG_we = command[26];
  //   REG_data_out = command[27]; REG_path_in = command[28]; DATA_to_adr = command[29]; TEMP_out = command[30];
  //   SP_updown = command[31]; PC_toDataBus = command[33]; ACC_reset = resetCPU; ADR_reg_reset = resetCPU;
  //   cu_reset = resetCPU; MAR_reset = resetCPU; MDR_reset = resetCPU; PC_reset = resetCPU; REGFILE_reset = resetCPU;
  //   TEMP_reset = resetCPU; deb_ADR[31:0] = deb_AdrReg; deb_FlagReg[2:0] = debFlagReg;
  //   deb_postaA_Data[2:0] = deb_posta_A; deb_postaB_Data[2:0] = deb_posta_B; IR_data[31:0] = deb_IR;
  //   MDR_data[31:0] = deb_MDR

  // Notes on the sheet:
  //   inServiceRoutine
endmodule

module ALU (
  input  [31:0] inA,
  input  [31:0] inB,
  input  [3:0] I3B,
  output [31:0] ALU_out,
  output cmp_greater,
  output cmp_equal,
  output cmp_less
);

  wire adder_1_cout, subtractor_1_bout, undriven, undriven_2;
  wire [4:0] bit_extender_1_out;
  wire [31:0] adder_1_out, and_1_out, divider_1_out, multiplier_1_out, not_1_out, or_1_out, shifter_1_out,
       shifter_2_out, subtractor_1_out, xor_1_out;

  Bit_Extender #(.in_width(32), .out_width(5)) bit_extender_1 (.in(inB), .out(bit_extender_1_out));
  Adder #(.width(32)) adder_1 (.a(inA), .b(inB), .out(adder_1_out), .cin(undriven), .cout(adder_1_cout));
  Subtractor #(.width(32)) subtractor_1 (
    .a(inA), .b(inB), .out(subtractor_1_out), .bin(undriven_2), .bout(subtractor_1_bout));
  Multiplier #(.width(32)) multiplier_1 (.a(inA), .b(inB), .out(multiplier_1_out));  // open: cin, cout
  Divider #(.width(32)) divider_1 (.a(inA), .b(inB), .out(divider_1_out));  // open: upper, rem
  Comparator #(.width(32)) comparator_1 (.a(inA), .b(inB), .gt(cmp_greater), .eq(cmp_equal), .lt(cmp_less));
  Shifter #(.width(32)) shifter_1 (.in(inA), .\dist (bit_extender_1_out), .out(shifter_1_out));
  Shifter #(.shift("lr"), .width(32)) shifter_2 (.in(inA), .\dist (bit_extender_1_out), .out(shifter_2_out));
  assign and_1_out = inA & inB;  // AND_Gate and_1, 32 bits wide
  assign or_1_out = inA | inB;  // OR_Gate or_1, 32 bits wide
  assign xor_1_out = inA ^ inB;  // XOR_Gate xor_1, 32 bits wide
  assign not_1_out = ~inA;  // NOT_Gate not_1, 32 bits wide
  Multiplexer #(.select(4), .width(32)) multiplexer_1 (
    .in0(adder_1_out), .in1(subtractor_1_out), .in2(multiplier_1_out), .in3(divider_1_out), .in4(and_1_out),
    .in5(or_1_out), .in6(xor_1_out), .in7(not_1_out), .in9(shifter_1_out), .in10(shifter_2_out),
    .out(ALU_out), .sel(I3B));  // open: in8, in11, in12, in13, in14, in15
endmodule

module RegisterFile (
  input  CLK,
  input  [31:0] inData,
  input  WE,
  input  [2:0] REG_inSel,
  input  [2:0] REG_outSel,
  input  OUT_enb,
  input  up_down,
  input  sp_enb,
  input  reset,
  output [31:0] deb_reg0,
  output [31:0] deb_reg1,
  output [31:0] deb_reg2,
  output [31:0] deb_reg3,
  output [31:0] deb_reg4,
  output [31:0] deb_reg5,
  output [31:0] deb_reg6,
  output [31:0] deb_reg7,
  output [31:0] regOut
);

  wire demultiplexer_1_out0, demultiplexer_1_out1, demultiplexer_1_out2, demultiplexer_1_out3,
       demultiplexer_1_out4, demultiplexer_1_out5, demultiplexer_1_out6, demultiplexer_1_out7;

  Demultiplexer #(.select(3)) demultiplexer_1 (
    .out0(demultiplexer_1_out0), .out1(demultiplexer_1_out1), .out2(demultiplexer_1_out2),
    .out3(demultiplexer_1_out3), .out4(demultiplexer_1_out4), .out5(demultiplexer_1_out5),
    .out6(demultiplexer_1_out6), .out7(demultiplexer_1_out7), .in(WE), .sel(REG_inSel));
  Register #(.width(32)) reg0 (.D(inData), .en(demultiplexer_1_out0), .clk(CLK), .Q(deb_reg0), .clr(reset));
  Register #(.width(32)) reg1 (.D(inData), .en(demultiplexer_1_out1), .clk(CLK), .Q(deb_reg1), .clr(reset));
  Register #(.width(32)) reg2 (.D(inData), .en(demultiplexer_1_out2), .clk(CLK), .Q(deb_reg2), .clr(reset));
  Register #(.width(32)) reg3 (.D(inData), .en(demultiplexer_1_out3), .clk(CLK), .Q(deb_reg3), .clr(reset));
  Register #(.width(32)) reg4 (.D(inData), .en(demultiplexer_1_out4), .clk(CLK), .Q(deb_reg4), .clr(reset));
  Register #(.width(32)) reg5 (.D(inData), .en(demultiplexer_1_out5), .clk(CLK), .Q(deb_reg5), .clr(reset));
  Register #(.width(32)) reg6 (.D(inData), .en(demultiplexer_1_out6), .clk(CLK), .Q(deb_reg6), .clr(reset));
  Counter #(.max('hffffffff), .width(32)) StackReg (
    .load(demultiplexer_1_out7), .D(inData), .count(sp_enb), .Q(deb_reg7), .up(up_down), .clk(CLK),
    .clr(reset));  // open: carry
  Multiplexer #(.enable("true"), .select(3), .width(32)) multiplexer_1 (
    .in0(deb_reg0), .in1(deb_reg1), .in2(deb_reg2), .in3(deb_reg3), .in4(deb_reg4), .in5(deb_reg5),
    .in6(deb_reg6), .in7(deb_reg7), .out(regOut), .sel(REG_outSel), .en(OUT_enb));
endmodule

module ControlUnit (
  input  isr_active,
  input  CLK,
  input  reset,
  input  [31:0] IR_in,
  input  interrupt,
  input  int_mask,
  input  [2:0] flag_reg,
  output [2:0] sp_sel,
  output int_postaMUX,
  output int_load,
  output int_pc_enb,
  output int_mar,
  output isr_we,
  output int_mask_cls,
  output ir_clear,
  output int_mask_we,
  output [31:0] int_jmp_adr,
  output isr_clear,
  output [34:0] controlBits,
  output [2:0] posta,
  output [2:0] deb_posta_A,
  output [2:0] deb_posta_B
);

  wire and_2_out, and_4_out, and_5_out, and_6_out, and_7_out, and_9_out, and_10_out, and_11_out, and_12_out,
       and_13_out, and_14_out, and_15_out, and_16_out, and_17_out, and_18_out, comparator_1_eq,
       comparator_2_eq, comparator_4_eq, creset, decoder_1_out2, decoder_2_out3, fetch_t0, fetch_t4,
       jmpdecoder_1_op_je, jmpdecoder_1_op_jgt, jmpdecoder_1_op_jlt, jmpdecoder_1_op_jne, key_int_spout,
       kwait, or_3_out, or_5_out, or_6_out, or_7_out, POSTA_A_out, POSTA_A_we, POSTA_B_out, POSTA_B_we;
  wire [3:0] counter_1_q, counter_2_q;
  wire [7:0] counter_3_q, rom_1_data;
  wire [9:0] bitselector_1_out;
  wire [34:0] int_mar_sp, rom_2_data;

  or or_1 (int_mask_cls, isr_we, comparator_1_eq);
  or or_2 (ir_clear, isr_we, and_2_out);
  Comparator #(.mode("unsigned")) comparator_1 (.a(IR_in[31:24]), .b(8'hb), .eq(comparator_1_eq));  // open: gt, lt
  Comparator #(.mode("unsigned")) comparator_2 (.a(IR_in[31:24]), .b(8'ha), .eq(comparator_2_eq));  // open: gt, lt
  Comparator #(.mode("unsigned")) comparator_3 (.a(IR_in[31:24]), .b(8'h9), .eq(kwait));  // open: gt, lt
  Comparator #(.mode("unsigned")) comparator_4 (.a(IR_in[31:24]), .b(8'h4), .eq(comparator_4_eq));  // open: gt, lt
  or or_3 (or_3_out, comparator_1_eq, comparator_2_eq);
  or or_4 (int_mask_we, comparator_2_eq, kwait);
  and and_1 (isr_clear, isr_active, comparator_4_eq);
  and and_2 (and_2_out, or_3_out, fetch_t4);
  ROM #(.addrWidth(11)) rom_1 (.addr({IR_in[31:24], IR_in[17:15]}), .data(rom_1_data));
  and and_3 (creset, or_3_out, fetch_t4);
  assign sp_sel = int_postaMUX ? 3'b111 : 3'bz;  // Controlled_Buffer controlled_buffer_1
  assign int_mar_sp = int_postaMUX ? 35'h2a008004 : 35'bz;  // Controlled_Buffer controlled_buffer_2
  assign int_mar_sp = decoder_1_out2 ? 35'h281000002 : 35'bz;  // Controlled_Buffer controlled_buffer_3
  or or_5 (or_5_out, int_load, int_mar, isr_we);
  assign int_mar_sp = or_5_out ? {35{1'b0}} : 35'bz;  // Controlled_Buffer controlled_buffer_4
  Register #(.width(3)) postaA (.D(IR_in[23:21]), .en(POSTA_A_we), .clk(CLK), .Q(deb_posta_A));  // open: clr
  Register #(.width(3)) postaB (.D(IR_in[20:18]), .en(POSTA_B_we), .clk(CLK), .Q(deb_posta_B));  // open: clr
  and and_4 (and_4_out, CLK, ~isr_active, key_int_spout);  // AND_Gate
  Counter #(.max('hf), .width(4)) counter_1 (
    .Q(counter_1_q), .clk(and_4_out), .clr(and_5_out));  // open: load, D, count, carry, up
  and and_5 (and_5_out, CLK, isr_active);
  Counter #(.max('hf), .width(4)) counter_2 (
    .Q(counter_2_q), .clk(and_6_out), .clr(or_6_out));  // open: load, D, count, carry, up
  and and_6 (and_6_out, ~kwait, and_7_out);  // AND_Gate
  and and_7 (and_7_out, CLK, ~key_int_spout);  // AND_Gate
  and and_8 (key_int_spout, fetch_t0, ~isr_active, and_11_out);  // AND_Gate
  Decoder #(.enable("false"), .select(4)) decoder_1 (
    .out1(int_postaMUX), .out2(decoder_1_out2), .out3(int_load), .out4(int_mar), .out5(isr_we),
    .sel(counter_1_q));  // open: out0, out6, out7, out8, out9, out10, out11, out12, out13, out14, out15
  Decoder #(.enable("false"), .select(4)) decoder_2 (
    .out0(fetch_t0), .out3(decoder_2_out3), .out4(fetch_t4), .sel(counter_2_q));  // open: out1, out2, out5, out6, out7, out8, out9, out10, out11, out12, out13, out14, out15
  and and_9 (and_9_out, ~kwait, and_10_out);  // AND_Gate
  // Digital_Oscilloscope #(.nState(35)) digital_oscilloscope_1: pin names not known; wires that end beside it: and_4_out, isr_we
  Counter counter_3 (
    .load(decoder_2_out3), .D(rom_1_data), .Q(counter_3_q), .clk(and_9_out), .clr(or_6_out));  // open: count, carry, up
  and and_10 (and_10_out, ~key_int_spout, CLK);  // AND_Gate
  and and_11 (and_11_out, interrupt, int_mask);
  assign posta = POSTA_A_out ? deb_posta_A : 3'bz;  // Controlled_Buffer controlled_buffer_5
  assign posta = POSTA_B_out ? deb_posta_B : 3'bz;  // Controlled_Buffer controlled_buffer_6
  and and_12 (and_12_out, kwait, and_11_out);
  assign int_jmp_adr = key_int_spout ? 32'h150 : 32'bz;  // Controlled_Buffer controlled_buffer_7
  or or_6 (or_6_out, creset, reset, and_14_out, and_13_out, and_12_out);
  ROM #(.dataWidth(35)) rom_2 (.addr(counter_3_q), .data(rom_2_data));
  and and_13 (and_13_out, ~bitselector_1_out[7], ~bitselector_1_out[6], bitselector_1_out[5], ~bitselector_1_out[4], ~bitselector_1_out[3], ~bitselector_1_out[2], ~bitselector_1_out[1], ~bitselector_1_out[0]);  // AND_Gate
  BitSelector #(.group(14), .width(35)) bitselector_1 (
    .in(rom_2_data), .out({POSTA_B_out, POSTA_B_we, POSTA_A_out, POSTA_A_we, bitselector_1_out}), .sel(2'b00));
  JmpDecoder jmpdecoder_1 (
    .opcode(IR_in[31:24]), .op_JNE(jmpdecoder_1_op_jne), .op_JE(jmpdecoder_1_op_je),
    .op_JGT(jmpdecoder_1_op_jgt), .op_JLT(jmpdecoder_1_op_jlt));
  and and_14 (and_14_out, decoder_2_out3, or_7_out);
  and and_15 (and_15_out, flag_reg[1], jmpdecoder_1_op_jne);
  or or_7 (or_7_out, and_15_out, and_16_out, and_17_out, and_18_out);
  and and_16 (and_16_out, ~flag_reg[1], jmpdecoder_1_op_je);  // AND_Gate
  and and_17 (and_17_out, ~flag_reg[2], jmpdecoder_1_op_jgt);  // AND_Gate
  Multiplexer #(.width(35)) multiplexer_1 (.in0(rom_2_data), .in1(int_mar_sp), .out(controlBits), .sel(key_int_spout));
  and and_18 (and_18_out, ~flag_reg[0], jmpdecoder_1_op_jlt);  // AND_Gate

  assign int_pc_enb = int_mar;

  // Notes on the sheet:
  //   MR
  //   MWE
  //   Kwait
  //   RET
  //   contents of rom_1 (hex, n*v repeats v):
  //   9*0 5 9 f 6*0 14 5*0 4e 0 0 54 4*0 48 8*0 44 6*0 41 15*0 19 15*0 59 7*0 5b 40*0 1d 2d 0 0 28 0 0 0
  //   1d 2d 0 0 28 0 0 0 1d 2d 0 0 28 0 0 0 1d 2d 0 0 28 7*0 28 7*0 28 7*0 28 0 0 38 8*0 23 0 0 0 34 7*0
  //   28 7*0 28 0 0 3d 7*0 3d 7*0 3d 7*0 3d 7*0 3d
  //   //mar = stackpointer
  //   //ram[stackpointer] = return adr
  //   fetch_t0 == true && key_int == true
  //   contents of rom_2 (hex, n*v repeats v):
  //   8008 21 c0 0 20 9008 21 4002040 20 9008 10001 28004 21 4002040 20 1400 2a00a004 21 4000840 20 9008
  //   10001 28004 a002002 20 1400 2002200 44000800 20 9008 21 2002200 c80040 4202000 20 9008 21 2002200
  //   480040 20 1400 2000a00 2882000 4200800 20 9008 10001 28004 2002221 c80040 4202000 20 1400 2000a00
  //   2082000 20 1000 2002200 2882000 4202000 20 8008 10001 20010 20 400 3000800 20 1400 2a008804 8b002002
  //   20 400 3000800 2a008804 21 20000058 20 8408 21 2a008804 281000002 20000058 20 1400 2a008804
  //   281000002 2a002018 20 0 20 0 20
  //   0: <
  //   1 : ==
  //   2 : >
  //   jne !=
  //   je ==
  //   jgt >
  //   jlt <
endmodule

module JmpDecoder (
  input  [7:0] opcode,
  output op_JNE,
  output op_JE,
  output op_JGT,
  output op_JLT
);

  Comparator comparator_1 (.a(opcode), .b(8'h1c), .eq(op_JNE));  // open: gt, lt
  Comparator comparator_2 (.a(opcode), .b(8'h1d), .eq(op_JE));  // open: gt, lt
  Comparator comparator_3 (.a(opcode), .b(8'h1e), .eq(op_JGT));  // open: gt, lt
  Comparator comparator_4 (.a(opcode), .b(8'h1f), .eq(op_JLT));  // open: gt, lt
endmodule

module GPU (
  input  CLK,
  input  kmt_we,
  input  color_we,
  input  posx_we,
  input  posy_we,
  input  [31:0] Data,
  output [1:0] deb_kmt,
  output [3:0] out_color,
  output [4:0] deb_posx,
  output [4:0] deb_posy
);

  wire and_1_out, and_2_out, decoder_1_out1, decoder_2_out5, decoder_2_out7, register_1_q;
  wire [3:0] counter_1_q;

  Register #(.width(2)) kmt (.D(Data[1:0]), .en(kmt_we), .clk(CLK), .Q(deb_kmt), .clr(and_1_out));
  Register #(.width(4)) color (.D(Data[3:0]), .en(color_we), .clk(CLK), .Q(out_color));  // open: clr
  Register #(.width(5)) posx_t (.D(Data[4:0]), .en(posx_we), .clk(CLK), .Q(deb_posx));  // open: clr
  Register #(.width(5)) posy_t (.D(Data[4:0]), .en(posy_we), .clk(CLK), .Q(deb_posy));  // open: clr
  Decoder #(.enable("false"), .select(2)) decoder_1 (.out1(decoder_1_out1), .sel(deb_kmt));  // open: out0, out2, out3
  Counter #(.max('hf), .width(4)) counter_1 (.Q(counter_1_q), .clk(CLK));  // open: load, D, count, carry, up, clr
  Decoder #(.enable("false"), .select(4)) decoder_2 (
    .out5(decoder_2_out5), .out7(decoder_2_out7), .sel(counter_1_q));  // open: out0, out1, out2, out3, out4, out6, out8, out9, out10, out11, out12, out13, out14, out15
  and and_1 (and_1_out, decoder_2_out7, register_1_q, decoder_1_out1);
  and and_2 (and_2_out, decoder_1_out1, decoder_2_out5);
  Register #(.width(1)) register_1 (.D(and_2_out), .en(and_2_out), .clk(CLK), .Q(register_1_q));  // open: clr

  // Notes on the sheet:
  //   px
  //   py
endmodule
