// Logisim project keyboardTest_t0.circ as structural Verilog: 1 circuit, main circuit main
module main (
  input  in_1,
  input  in_2,
  input  in_3,
  input  in_4,
  input  in_5,
  input  in_6,
  input  in_7,
  input  in_8,
  output [6:0] out_9,
  output [7:0] out_10
);

  wire clock_1_out, keyboard_1_avail;
  wire [7:0] counter_1_q, multiplexer_1_out, multiplier_1_out, ram_1_dout, register_1_q, register_2_q;

  Clock clock_1 (.out(clock_1_out));
  Keyboard keyboard_1 (.clk(clock_1_out), .re(keyboard_1_avail), .clr(in_1), .avail(keyboard_1_avail), .data(out_9));
  Subtractor subtractor_1 (.a({1'b0, out_9}), .b(8'h30), .out(out_10));  // open: bin, bout
  Counter counter_1 (
    .load(in_5), .D(8'h3), .Q(counter_1_q), .up(in_3), .clk(clock_1_out), .clr(in_2));  // open: count, carry
  Multiplexer #(.width(8)) multiplexer_1 (.in0(out_10), .in1(counter_1_q), .out(multiplexer_1_out), .sel(in_8));
  RAM #(.asyncread("true"), .\type ("nonvolatile")) ram_1 (
    .addr(counter_1_q), .we(in_6), .clk(clock_1_out), .din(multiplexer_1_out), .dout(ram_1_dout));  // open: oe
  Register register_1 (.D(ram_1_dout), .en(in_4), .clk(clock_1_out), .Q(register_1_q));  // open: clr
  Register register_2 (.D(ram_1_dout), .Q(register_2_q));  // open: en, clk, clr
  assign ram_1_dout = in_7 ? register_2_q : 8'bz;  // Controlled_Buffer controlled_buffer_1
  Multiplier multiplier_1 (.a(register_2_q), .out(multiplier_1_out));  // open: b, cin, cout
  Register register_3 (.D(multiplier_1_out), .Q(ram_1_dout));  // open: en, clk, clr
endmodule
