// Logisim project t1_keyboardInput.circ as structural Verilog: 1 circuit, main circuit main
module main (
  input  adr_bus,
  input  in_2,
  input  in_3,
  input  in_4,
  input  in_5
);

  wire and_1_out, and_2_out, clock_1_out, comparator_1_eq, counter_2_carry, decoder_1_out0, decoder_1_out1,
       Interrupt_q, keyboard_1_avail;
  wire [2:0] controlled_buffer_1_out, ram_1_dout;
  wire [3:0] adder_1_out, controlled_buffer_1_out_2, counter_3_q;
  wire [5:0] counter_1_q, counter_2_q;
  wire [6:0] keyboard_1_data;
  wire [9:0] multiplexer_1_out;
  wire [12:0] rom_1_data;

  Counter #(.max('h3f), .width(6)) counter_1 (
    .count(and_1_out), .Q(counter_1_q), .clk(clock_1_out), .clr(in_3));  // open: load, D, carry, up
  and and_1 (and_1_out, in_2, ~comparator_1_eq);  // AND_Gate
  Comparator #(.width(6)) comparator_1 (.a(counter_1_q), .b(6'b100100), .eq(comparator_1_eq));  // open: gt, lt
  Decoder #(.enable("false")) decoder_1 (.out0(decoder_1_out0), .out1(decoder_1_out1), .sel(adr_bus));
  ROM #(.addrWidth(6), .dataWidth(13)) rom_1 (.addr(counter_1_q), .data(rom_1_data));
  Clock clock_1 (.out(clock_1_out));
  and and_2 (and_2_out, clock_1_out, Interrupt_q);
  Keyboard keyboard_1 (.clk(and_2_out), .re(1'b1), .avail(keyboard_1_avail), .data(keyboard_1_data));  // open: clr
  assign {controlled_buffer_1_out_2, controlled_buffer_1_out} = decoder_1_out0 ? keyboard_1_data : 7'bz;  // Controlled_Buffer controlled_buffer_1
  Register #(.width(1)) Interrupt (.D(keyboard_1_avail), .en(1'b1), .clk(clock_1_out), .Q(Interrupt_q));  // open: clr
  Hex_Digit_Display hex_digit_display_1 (.value(controlled_buffer_1_out_2));  // open: dp
  Hex_Digit_Display hex_digit_display_2 (.value({1'b0, controlled_buffer_1_out}));  // open: dp
  Multiplexer #(.width(10)) multiplexer_1 (
    .in0({counter_3_q, counter_2_q}), .in1(rom_1_data[9:0]), .out(multiplexer_1_out), .sel(in_4));
  RAM #(.addrWidth(10), .dataWidth(3)) ram_1 (
    .addr(multiplexer_1_out), .we(in_5), .oe(1'b1), .clk(clock_1_out), .din(rom_1_data[12:10]),
    .dout(ram_1_dout));
  Adder #(.width(4)) adder_1 (.a(rom_1_data[3:0]), .b(4'b0110), .out(adder_1_out));  // open: cin, cout
  Counter #(.max('h3f), .width(6)) counter_2 (
    .Q(counter_2_q), .carry(counter_2_carry), .clk(clock_1_out));  // open: load, D, count, up, clr
  Counter #(.max('hf), .width(4)) counter_3 (
    .count(counter_2_carry), .Q(counter_3_q), .clk(clock_1_out));  // open: load, D, carry, up, clr
  // RGB_Video #(.height(16), .scale(8), .width(64)) rgb_video_1: pin names not known; wires that end beside it: {controlled_buffer_1_out_2, controlled_buffer_1_out}, clock_1_out, 1'b1, counter_2_q, counter_3_q, ram_1_dout

  // Notes on the sheet:
  //   MemoryMap I/O Decoder
  //   contents of rom_1 (hex, n*v repeats v):
  //   0 401 402 403 4 5 440 41 42 43 444 45 480 481 482 483 484 85 4c0 c1 c2 c3 4c4 c5 500 101 102 103 504
  //   105 140 141 142 143 144 145
  //   DataBus
  //   CPU
endmodule
