// Logisim project t2_simpleCalcV0.circ as structural Verilog: 1 circuit, main circuit main
module main (
);

  wire and_1_out, clock_1_out, comparator_1_eq, decoder_1_out0, decoder_1_out2, decoder_1_out3,
       keyboard_1_avail;
  wire [2:0] counter_1_q;
  wire [6:0] adder_1_out, adder_2_out, keyboard_1_data, multiplexer_1_out, register_1_q, register_2_q,
       register_3_q, subtractor_1_out;

  Clock clock_1 (.out(clock_1_out));
  Keyboard keyboard_1 (
    .clk(clock_1_out), .re(keyboard_1_avail), .avail(keyboard_1_avail), .data(keyboard_1_data));  // open: clr
  Register #(.width(7)) register_1 (
    .D(adder_2_out), .en(decoder_1_out2), .clk(clock_1_out), .Q(register_1_q));  // open: clr
  and and_1 (and_1_out, keyboard_1_avail, clock_1_out);
  Multiplexer #(.width(7)) multiplexer_1 (
    .in0(keyboard_1_data), .in1(adder_1_out), .out(multiplexer_1_out), .sel(decoder_1_out3));
  Counter #(.max('h7), .width(3)) counter_1 (.Q(counter_1_q), .clk(and_1_out));  // open: load, D, count, carry, up, clr
  Adder #(.width(7)) adder_1 (.a(7'b0110000), .b(register_1_q), .out(adder_1_out));  // open: cin, cout
  Register #(.width(7)) register_2 (
    .D(multiplexer_1_out), .en(clock_1_out), .clk(clock_1_out), .Q(register_2_q));  // open: clr
  Comparator #(.mode("unsigned"), .width(7)) comparator_1 (
    .a(keyboard_1_data), .b(7'b0100011), .eq(comparator_1_eq));  // open: gt, lt
  Decoder #(.select(3)) decoder_1 (
    .out0(decoder_1_out0), .out2(decoder_1_out2), .out3(decoder_1_out3), .sel(counter_1_q));  // open: out1, out4, out5, out6, out7, en
  Subtractor #(.width(7)) subtractor_1 (
    .a(keyboard_1_data), .b(7'b0110000), .out(subtractor_1_out));  // open: bin, bout
  TTY tty_1 (.data(register_2_q), .clk(clock_1_out), .clr(comparator_1_eq));  // open: we
  Register #(.width(7)) register_3 (
    .D(subtractor_1_out), .en(decoder_1_out0), .clk(clock_1_out), .Q(register_3_q));  // open: clr
  Adder #(.width(7)) adder_2 (.a(register_3_q), .b(subtractor_1_out), .out(adder_2_out));  // open: cin, cout

  // Notes on the sheet:
  //   2+5
  //   cikti: 2+57
  //   # clear
  //   int => ascii
  //   ascii => int
endmodule
