// Logisim project t3_simpleCalcV1.circ as structural Verilog: 2 circuits, main circuit main
module main (
  input  [8:0] in_1,
  input  [6:0] in_2,
  input  in_3,
  output [6:0] out_4,
  output isDigit
);

  wire adder_3_cout, and_1_out, and_2_out, clock_1_out, comparator_1_eq, comparator_2_lt, comparator_3_gt,
       decoder_1_out1, decoder_1_out2, decoder_1_out3, keyboard_1_avail, keyboard_2_avail, n7447_1_pin1,
       n7447_1_pin2, n7447_1_pin6, n7447_1_pin7, n7447_1_pin9, n7447_1_pin10, n7447_1_pin11, n7447_1_pin12,
       n7447_1_pin13, n7447_1_pin14, n7447_1_pin15, not_1_out, not_2_out, not_3_out, not_4_out, not_5_out,
       not_6_out, not_7_out, or_1_out, register_5_q, undriven;
  wire [2:0] counter_1_q;
  wire [3:0] register_4_q, register_4_q_2, register_4_q_3, register_4_q_4;
  wire [6:0] adder_1_out, adder_4_out, keyboard_1_data, multiplexer_1_out, register_2_q, subtractor_2_out;
  wire [15:0] adder_2_out, adder_5_out, bit_extender_1_out, multiplier_1_out, register_3_q;

  Clock clock_1 (.out(clock_1_out));
  Keyboard keyboard_1 (
    .clk(clock_1_out), .re(keyboard_1_avail), .avail(keyboard_1_avail), .data(keyboard_1_data));  // open: clr
  Keyboard keyboard_2 (.clk(clock_1_out), .re(keyboard_2_avail), .avail(keyboard_2_avail), .data(out_4));  // open: clr
  Register #(.width(16)) register_1 (.D(adder_2_out), .en(undriven), .clk(clock_1_out));  // open: Q, clr
  and and_1 (and_1_out, keyboard_2_avail, clock_1_out);
  Multiplexer #(.width(7)) multiplexer_1 (
    .in0(keyboard_1_data), .in1(adder_1_out), .out(multiplexer_1_out), .sel(decoder_1_out3));
  Counter #(.max('h7), .width(3)) counter_1 (.Q(counter_1_q), .clk(and_2_out));  // open: load, D, count, carry, up, clr
  and and_2 (and_2_out, and_1_out, ~isDigit);  // AND_Gate
  Adder #(.width(7)) adder_1 (.a(7'b0110000), .out(adder_1_out));  // open: b, cin, cout
  Register #(.width(7)) register_2 (
    .D(multiplexer_1_out), .en(clock_1_out), .clk(clock_1_out), .Q(register_2_q));  // open: clr
  Comparator #(.mode("unsigned"), .width(7)) comparator_1 (
    .a(keyboard_1_data), .b(7'b0100011), .eq(comparator_1_eq));  // open: gt, lt
  Decoder #(.select(3)) decoder_1 (
    .out1(decoder_1_out1), .out2(decoder_1_out2), .out3(decoder_1_out3), .sel(counter_1_q));  // open: out0, out4, out5, out6, out7, en
  Comparator #(.mode("unsigned"), .width(7)) comparator_2 (
    .a(out_4), .b(7'b0110000), .lt(comparator_2_lt));  // open: gt, eq
  Comparator #(.mode("unsigned"), .width(7)) comparator_3 (
    .a(out_4), .b(7'b0111001), .gt(comparator_3_gt));  // open: eq, lt
  Subtractor #(.width(7)) subtractor_1 (.a(keyboard_1_data), .b(7'b0110000));  // open: out, bin, bout
  and and_3 (isDigit, ~comparator_2_lt, ~comparator_3_gt);  // AND_Gate
  TTY tty_1 (.data(register_2_q), .clk(clock_1_out), .clr(comparator_1_eq));  // open: we
  Register #(.width(16)) register_3 (
    .D({register_4_q_4, register_4_q_3, register_4_q_2, register_4_q}), .en(decoder_1_out1),
    .clk(clock_1_out), .Q(register_3_q));  // open: clr
  Subtractor #(.width(7)) subtractor_2 (.a(out_4), .b(7'b0110000), .out(subtractor_2_out));  // open: bin, bout
  Adder #(.width(16)) adder_2 (
    .a(register_3_q), .b({register_4_q_4, register_4_q_3, register_4_q_2, register_4_q}), .out(adder_2_out));  // open: cin, cout
  assign bit_extender_1_out = {{9{subtractor_2_out[6]}}, subtractor_2_out};  // Bit_Extender bit_extender_1
  Register #(.width(16)) register_4 (
    .D(adder_5_out), .en(isDigit), .clk(clock_1_out),
    .Q({register_4_q_4, register_4_q_3, register_4_q_2, register_4_q}), .clr(or_1_out));
  or or_1 (or_1_out, decoder_1_out2, adder_3_cout);
  Hex_Digit_Display hex_digit_display_1 (.value(register_4_q_4));  // open: dp
  Hex_Digit_Display hex_digit_display_2 (.value(register_4_q_3));  // open: dp
  Adder #(.width(16)) adder_3 (
    .a({register_4_q_4, register_4_q_3, register_4_q_2, register_4_q}), .b(16'h1), .cout(adder_3_cout));  // open: out, cin
  Hex_Digit_Display hex_digit_display_3 (.value(register_4_q_2));  // open: dp
  Hex_Digit_Display hex_digit_display_4 (.value(register_4_q));  // open: dp
  Adder #(.width(7)) adder_4 (.a(7'b0110000), .b(in_2), .out(adder_4_out));  // open: cin, cout
  Multiplier #(.width(16)) multiplier_1 (
    .a({register_4_q_4, register_4_q_3, register_4_q_2, register_4_q}), .b(16'ha), .out(multiplier_1_out));  // open: cin, cout
  Adder #(.width(16)) adder_5 (.a(bit_extender_1_out), .b(multiplier_1_out), .out(adder_5_out));  // open: cin, cout
  Register #(.width(1)) register_5 (
    .D(adder_3_cout), .en(adder_3_cout), .clk(clock_1_out), .Q(register_5_q));  // open: clr
  TTY tty_2 (.data(adder_4_out), .clk(in_3));  // open: we, clr
  not not_1 (not_1_out, n7447_1_pin15);
  not not_2 (not_2_out, n7447_1_pin14);
  not not_3 (not_3_out, n7447_1_pin13);
  _7447 #(.ShowInternalStructure("true")) u_7447_1 (
    .pin1(n7447_1_pin1), .pin2(n7447_1_pin2), .pin6(n7447_1_pin6), .pin7(n7447_1_pin7),
    .pin15(n7447_1_pin15), .pin14(n7447_1_pin14), .pin13(n7447_1_pin13), .pin12(n7447_1_pin12),
    .pin11(n7447_1_pin11), .pin10(n7447_1_pin10), .pin9(n7447_1_pin9));  // open: pin3, pin4, pin5
  decToBCD dectobcd_1 (
    .inp_1(in_1[0]), .inp_2(in_1[1]), .inp_3(in_1[2]), .inp_4(in_1[3]), .inp_5(in_1[4]), .inp_6(in_1[5]),
    .inp_7(in_1[6]), .inp_8(in_1[7]), .inp_9(in_1[8]), .out_a(n7447_1_pin7), .out_b(n7447_1_pin1),
    .out_c(n7447_1_pin2), .out_d(n7447_1_pin6));
  _7_Segment_Display u_7_segment_display_1 (
    .g(not_2_out), .f(not_1_out), .a(not_3_out), .b(not_4_out), .e(not_7_out), .d(not_6_out), .c(not_5_out));  // open: dp
  not not_4 (not_4_out, n7447_1_pin12);
  not not_5 (not_5_out, n7447_1_pin11);
  not not_6 (not_6_out, n7447_1_pin10);
  not not_7 (not_7_out, n7447_1_pin9);

  // Notes on the sheet:
  //   2+5
  //   cikti: 2+57
  //   # clear
  //   int => ascii
  //   ascii => int
  //   145
  //   ascii => int
  //   int n = n * 10 + key
  //   0 * 10 + 1 = 1
  //   1 * 10 + 4 = 14
  //   14 * 10 + 5 = 145
endmodule

module decToBCD (
  input  inp_1,
  input  inp_2,
  input  inp_3,
  input  inp_4,
  input  inp_5,
  input  inp_6,
  input  inp_7,
  input  inp_8,
  input  inp_9,
  output out_a,
  output out_b,
  output out_c,
  output out_d
);

  or or_1 (out_d, inp_9, inp_8);
  or or_2 (out_c, inp_7, inp_6, inp_5, inp_4);
  or or_3 (out_b, inp_6, inp_5, inp_3, inp_2);
  or or_4 (out_a, inp_9, inp_7, inp_5, inp_3, inp_1);
endmodule
