// Logisim project t0_clearScreen.circ as structural Verilog
module main (
);

  wire and_1_out, and_2_out, and_3_out, and_4_out, and_5_out, and_6_out, and_7_out, clock_1_out,
       counter_1_carry, rgb_video_1_p1;
  wire [3:0] counter_1_q, counter_2_q;

  Clock clock_1 (.out(clock_1_out));
  Counter #(.max('hf), .width(4)) counter_1 (
    .Q(counter_1_q), .carry(counter_1_carry), .clk(clock_1_out));  // open: load, D, count, up, clr
  Counter #(.max('hf), .width(4)) counter_2 (
    .count(counter_1_carry), .Q(counter_2_q), .clk(clock_1_out));  // open: load, D, carry, up, clr
  // RGB_Video #(.cursor("No Cursor"), .height(16), .scale(8), .width(16)) rgb_video_1: pin names not known; wires that end beside it: rgb_video_1_p1, clock_1_out, 1'b1, counter_1_q, counter_2_q, 3'b001
  and and_1 (and_1_out, counter_2_q[0], counter_1_q[0]);
  and and_2 (and_2_out, counter_2_q[1], counter_1_q[1]);
  and and_3 (and_3_out, counter_2_q[2], counter_1_q[2]);
  and and_4 (and_4_out, counter_2_q[3], counter_1_q[3]);
  and and_5 (and_5_out, and_1_out, and_2_out);
  and and_6 (and_6_out, and_3_out, and_4_out);
  and and_7 (and_7_out, and_5_out, and_6_out);
  Register #(.width(1)) register_1 (
    .D(and_7_out), .en(and_7_out), .clk(clock_1_out), .Q(rgb_video_1_p1), .clr(rgb_video_1_p1));

  // Notes on the sheet:
  //   111 w 000 b
  //   1 tik reset sinyalini geciktirmek icin
endmodule

module ALU (
  input  [7:0] A,
  input  [7:0] B,
  input  [2:0] shiftAmount,
  input  [2:0] aluMux,
  input  aluMuxEnb,
  output [7:0] outALU
);

  wire [7:0] adder_1_out, and_1_out, not_1_out, or_1_out, shifter_1_out, shifter_2_out, subtractor_1_out,
       xor_1_out;

  Adder adder_1 (.a(A), .b(B), .out(adder_1_out));  // open: cin, cout
  Subtractor subtractor_1 (.a(A), .b(B), .out(subtractor_1_out));  // open: bin, bout
  Shifter shifter_1 (.in(A), .\dist (shiftAmount), .out(shifter_1_out));
  Shifter #(.shift("lr")) shifter_2 (.in(A), .\dist (shiftAmount), .out(shifter_2_out));
  assign not_1_out = ~B;  // NOT_Gate not_1, 8 bits wide
  assign and_1_out = A & B;  // AND_Gate and_1, 8 bits wide
  assign or_1_out = B | B;  // OR_Gate or_1, 8 bits wide
  assign xor_1_out = A ^ B;  // XOR_Gate xor_1, 8 bits wide
  Multiplexer #(.enable("true"), .select(3), .width(8)) multiplexer_1 (
    .in0(adder_1_out), .in1(subtractor_1_out), .in2(shifter_1_out), .in3(shifter_2_out), .in4(and_1_out),
    .in5(or_1_out), .in6(not_1_out), .in7(xor_1_out), .out(outALU), .sel(aluMux), .en(aluMuxEnb));
endmodule
