// Logisim project t1_drawingMultiROM.circ as structural Verilog: 1 circuit, main circuit main
module main (
  input  [1:0] in_1,
  input  [1:0] in_2
);

  wire clock_1_out, clock_2_out, counter_1_carry;
  wire [1:0] or_1_out;
  wire [2:0] multiplexer_1_out, rom_1_data, rom_2_data, rom_3_data, rom_4_data;
  wire [3:0] counter_1_q, counter_2_q;
  wire [7:0] demultiplexer_1_out0, demultiplexer_1_out1, demultiplexer_1_out2, demultiplexer_1_out3;

  assign or_1_out = in_1 | in_2;  // OR_Gate or_1, 2 bits wide
  Demultiplexer #(.select(2), .width(8)) demultiplexer_1 (
    .out0(demultiplexer_1_out0), .out1(demultiplexer_1_out1), .out2(demultiplexer_1_out2),
    .out3(demultiplexer_1_out3), .in({counter_2_q, counter_1_q}), .sel(or_1_out));
  ROM #(.dataWidth(3)) rom_1 (.addr(demultiplexer_1_out3), .data(rom_1_data));
  ROM #(.dataWidth(3)) rom_2 (.addr(demultiplexer_1_out2), .data(rom_2_data));
  ROM #(.dataWidth(3)) rom_3 (.addr(demultiplexer_1_out1), .data(rom_3_data));
  ROM #(.dataWidth(3)) rom_4 (.addr(demultiplexer_1_out0), .data(rom_4_data));
  Clock clock_1 (.out(clock_1_out));
  Counter #(.max('hf), .width(4)) counter_1 (
    .Q(counter_1_q), .carry(counter_1_carry), .clk(clock_1_out));  // open: load, D, count, up, clr
  Counter #(.max('hf), .width(4)) counter_2 (
    .count(counter_1_carry), .Q(counter_2_q), .clk(clock_1_out));  // open: load, D, carry, up, clr
  Multiplexer #(.select(2), .width(3)) multiplexer_1 (
    .in0(rom_4_data), .in1(rom_3_data), .in2(rom_2_data), .in3(rom_1_data), .out(multiplexer_1_out),
    .sel(or_1_out));
  // RGB_Video #(.height(16), .scale(8), .width(16)) rgb_video_1: pin names not known; wires that end beside it: clock_1_out, 1'b1, counter_1_q, counter_2_q, multiplexer_1_out
  Clock clock_2 (.out(clock_2_out));

  // Notes on the sheet:
  //   contents of rom_1 (hex, n*v repeats v):
  //   17*0 14*1 0 0 1 12*2 1 0 0 1 2 10*3 2 1 0 0 1 2 3 8*4 3 2 1 0 0 1 2 3 4 6*5 4 3 2 1 0 0 1 2 3 4 5
  //   4*6 5 4 3 2 1 0 0 1 2 3 4 6*5 4 3 2 1 0 0 1 2 3 8*4 3 2 1 0 0 1 2 10*3 2 1 0 0 1 12*2 1 0 0 14*1
  //   18*0 7 2 7 3 7 4 7 5 7 6 7 1 7 4 0 0 7 2 7 3 7 4 7 5 7 6 7 1 7 4
  //   contents of rom_2 (hex, n*v repeats v):
  //   32*1 32*2 32*3 32*4 32*5 32*6 32*7
  //   contents of rom_3 (hex, n*v repeats v):
  //   4*0 8*1 7*0 1 8*0 1 5*0 1 0 0 0 4*1 0 0 0 1 0 0 0 1 0 0 0 1 4*0 1 0 0 0 1 0 0 1 0 0 1 6*0 1 0 0 1 0
  //   0 1 0 0 1 0 0 3 3 0 0 1 0 0 1 0 0 1 0 0 1 0 0 3 3 0 0 1 0 0 1 0 0 1 0 0 1 0 0 3 3 0 0 1 0 0 1 0 0 1
  //   0 0 1 0 0 3 3 0 0 1 0 0 1 0 0 1 0 0 1 0 0 3 3 0 0 1 0 0 1 0 0 1 0 0 1 0 0 3 3 0 0 1 0 0 1 0 0 1 0 0
  //   1 0 0 3 3 0 0 1 0 0 1 0 0 1 0 0 1 0 0 3 3 0 0 1 0 0 1 0 0 1 0 0 1 0 0 3 3 0 0 1 0 0 1 0 0 2 0 0 2 0
  //   0 3 3 0 0 2 0 0 2
  //   contents of rom_4 (hex, n*v repeats v):
  //   17*0 2 10*0 2 2 4*0 2 2 7*0 2 0 2 4*0 2 0 2 5*0 2 0 0 2 4*0 2 0 0 5*2 0 0 0 2 4*0 2 9*0 2 5*0 2 8*0
  //   2 5*0 2 0 0 3 4*0 3 0 2 5*0 2 10*0 2 5*0 2 9*0 2 5*0 2 4*0 2 4*0 2 4*0 2 4*0 2 0 2 0 0 0 2 5*0 2 8*0
  //   2 6*0 9*2
endmodule
