// Logisim project t2_drawingScreen.circ as structural Verilog: 1 circuit, main circuit main
module main (
  input  [10:0] xyColor,
  input  Write,
  input  MUX_sel,
  input  CLK
);

  wire clock_1_out, clock_2_out, controlled_buffer_1_out, not_1_out, not_2_out, or_1_out, Xcounter_carry;
  wire [2:0] ram_1_dout;
  wire [3:0] Xcounter_q, Ycounter_q;
  wire [7:0] multiplexer_1_out;

  not not_1 (not_1_out, Write);
  RAM #(.dataWidth(3)) ram_1 (
    .addr(multiplexer_1_out), .we(Write), .oe(not_1_out), .clk(or_1_out), .din(xyColor[10:8]),
    .dout(ram_1_dout));
  Multiplexer #(.width(8)) multiplexer_1 (
    .in0({Ycounter_q, Xcounter_q}), .in1(xyColor[7:0]), .out(multiplexer_1_out), .sel(MUX_sel));
  Clock clock_1 (.out(clock_1_out));
  or or_1 (or_1_out, clock_1_out, CLK);
  Counter #(.max('hf), .width(4)) Xcounter (
    .Q(Xcounter_q), .carry(Xcounter_carry), .clk(controlled_buffer_1_out));  // open: load, D, count, up, clr
  assign controlled_buffer_1_out = not_2_out ? or_1_out : 1'bz;  // Controlled_Buffer controlled_buffer_1
  not not_2 (not_2_out, Write);
  Counter #(.max('hf), .width(4)) Ycounter (
    .count(Xcounter_carry), .Q(Ycounter_q), .clk(controlled_buffer_1_out));  // open: load, D, carry, up, clr
  // RGB_Video #(.height(16), .scale(8), .width(16)) rgb_video_1: pin names not known; wires that end beside it: controlled_buffer_1_out, 1'b1, Xcounter_q, Ycounter_q, ram_1_dout
  Clock clock_2 (.out(clock_2_out));
endmodule
