// Logisim project t3_gpuV0.circ as structural Verilog: 4 circuits, main circuit main
module main (
  input  in_1,
  input  [27:0] in_2,
  input  in_3,
  input  [7:0] x0,
  input  [7:0] x1,
  input  [7:0] y0,
  input  [7:0] y1
);

  wire clock_1_out, comparator_2_lt, decoder_1_out0, decoder_1_out1, decoder_1_out2, decoder_1_out3, undriven;
  wire [1:0] controlunit_1_out_3_2, controlunit_1_out_3_3, controlunit_1_out_3_4;
  wire [2:0] counter_1_q;
  wire [3:0] regfile_1_r0, regfile_1_r0_2, regfile_1_r0_3, regfile_1_r0_4, regfile_1_r1, regfile_1_r1_2,
       regfile_1_r1_3, regfile_1_r1_4, regfile_1_r2, regfile_1_r2_2, regfile_1_r2_3, regfile_1_r2_4,
       regfile_1_r3, regfile_1_r3_2, regfile_1_r3_3, regfile_1_r3_4;
  wire [5:0] alu_1_a_greaterb, register_5_q;
  wire [7:0] counter_2_q, deltaX_q, deltaY_q, divider_1_out, dy_dx_q, error_q, register_2_q, register_3_q,
       subtractor_1_out, subtractor_2_out;
  wire [9:0] controlunit_1_out_3;
  wire [15:0] alu_1_outalu, regfile_1_regout, register_1_q, register_4_q;

  controlUnit controlunit_1 (
    .CLK(in_1), .Instruction(in_2),
    .out_3({controlunit_1_out_3[9], controlunit_1_out_3_4, controlunit_1_out_3_3, controlunit_1_out_3[4], controlunit_1_out_3_2, controlunit_1_out_3[1:0]}));
  regFile regfile_1 (
    .CLK(in_1), .regData(register_4_q), .WE(controlunit_1_out_3[9]), .regSelect(controlunit_1_out_3_4),
    .outRegSel(controlunit_1_out_3_3), .regOut(regfile_1_regout),
    .r0({regfile_1_r0_4, regfile_1_r0_3, regfile_1_r0_2, regfile_1_r0}),
    .r1({regfile_1_r1_4, regfile_1_r1_3, regfile_1_r1_2, regfile_1_r1}),
    .r2({regfile_1_r2_4, regfile_1_r2_3, regfile_1_r2_2, regfile_1_r2}),
    .r3({regfile_1_r3_4, regfile_1_r3_3, regfile_1_r3_2, regfile_1_r3}));
  Hex_Digit_Display hex_digit_display_1 (.value(regfile_1_r0_4));  // open: dp
  Hex_Digit_Display hex_digit_display_2 (.value(regfile_1_r0_3));  // open: dp
  Register #(.width(16)) register_1 (
    .D(regfile_1_regout), .en(controlunit_1_out_3[4]), .clk(in_1), .Q(register_1_q));  // open: clr
  Hex_Digit_Display hex_digit_display_3 (.value(regfile_1_r0_2));  // open: dp
  Hex_Digit_Display hex_digit_display_4 (.value(regfile_1_r0));  // open: dp
  Hex_Digit_Display hex_digit_display_5 (.value(regfile_1_r1_4));  // open: dp
  Clock clock_1 (.out(clock_1_out));
  Hex_Digit_Display hex_digit_display_6 (.value(regfile_1_r1_3));  // open: dp
  Hex_Digit_Display hex_digit_display_7 (.value(regfile_1_r1_2));  // open: dp
  Register register_2 (.D(8'hf0), .en(decoder_1_out0), .clk(clock_1_out), .Q(register_2_q));  // open: clr
  Register register_3 (.D(8'h46), .en(decoder_1_out0), .clk(clock_1_out), .Q(register_3_q));  // open: clr
  Hex_Digit_Display hex_digit_display_8 (.value(regfile_1_r1));  // open: dp
  Hex_Digit_Display hex_digit_display_9 (.value(regfile_1_r2_4));  // open: dp
  Hex_Digit_Display hex_digit_display_10 (.value(regfile_1_r2_3));  // open: dp
  Hex_Digit_Display hex_digit_display_11 (.value(regfile_1_r2_2));  // open: dp
  ALU alu_1 (
    .A(register_1_q), .B(regfile_1_regout), .aluMux(controlunit_1_out_3_2),
    .aluMuxEnb(controlunit_1_out_3[1]), .outALU(alu_1_outalu), .A_greaterB(alu_1_a_greaterb[0]),
    .A_equalB(alu_1_a_greaterb[1]), .A_lessB(alu_1_a_greaterb[2]));
  Subtractor subtractor_1 (.a(register_2_q), .b(8'h64), .out(subtractor_1_out));  // open: bin, bout
  Subtractor subtractor_2 (.a({8{1'b0}}), .b(register_3_q), .out(subtractor_2_out));  // open: bin, bout
  Hex_Digit_Display hex_digit_display_12 (.value(regfile_1_r2));  // open: dp
  Hex_Digit_Display hex_digit_display_13 (.value(regfile_1_r3_4));  // open: dp
  Hex_Digit_Display hex_digit_display_14 (.value(regfile_1_r3_3));  // open: dp
  Hex_Digit_Display hex_digit_display_15 (.value(regfile_1_r3_2));  // open: dp
  Hex_Digit_Display hex_digit_display_16 (.value(regfile_1_r3));  // open: dp
  Register deltaX (.D(subtractor_1_out), .en(decoder_1_out1), .clk(clock_1_out), .Q(deltaX_q));  // open: clr
  Register deltaY (.D(subtractor_2_out), .en(decoder_1_out1), .clk(clock_1_out), .Q(deltaY_q));  // open: clr
  Register #(.width(16)) register_4 (
    .D(alu_1_outalu), .en(controlunit_1_out_3[0]), .clk(in_1), .Q(register_4_q));  // open: clr
  Divider #(.mode("twosComplement")) divider_1 (.a(deltaX_q), .b(deltaY_q), .out(divider_1_out));  // open: upper, rem
  Comparator #(.mode("unsigned"), .width(16)) comparator_1 (
    .a(register_4_q), .b({16{1'b1}}), .gt(alu_1_a_greaterb[3]), .eq(alu_1_a_greaterb[4]),
    .lt(alu_1_a_greaterb[5]));
  Register dy_dx (.D(divider_1_out), .en(decoder_1_out2), .clk(clock_1_out), .Q(dy_dx_q));  // open: clr
  Counter #(.max('h7), .width(3)) counter_1 (
    .Q(counter_1_q), .clk(clock_1_out));  // open: load, D, count, carry, up, clr
  Decoder #(.select(3)) decoder_1 (
    .out0(decoder_1_out0), .out1(decoder_1_out1), .out2(decoder_1_out2), .out3(decoder_1_out3),
    .sel(counter_1_q));  // open: out4, out5, out6, out7, en
  Counter counter_2 (
    .load(decoder_1_out3), .D(8'h64), .count(comparator_2_lt), .Q(counter_2_q), .clk(clock_1_out));  // open: carry, up, clr
  Register #(.width(6)) register_5 (.D(alu_1_a_greaterb), .en(undriven), .clk(in_1), .Q(register_5_q));  // open: clr
  Comparator #(.mode("unsigned")) comparator_2 (
    .a(counter_2_q), .b(register_2_q), .lt(comparator_2_lt));  // open: gt, eq
  Counter error (
    .load(decoder_1_out2), .D(dy_dx_q), .count(comparator_2_lt), .Q(error_q), .clk(clock_1_out));  // open: carry, up, clr

  // Notes on the sheet:
  //   (100,0) (240,70)
  //   R0
  //   R1
  //   R2
  //   R3
endmodule

module ALU (
  input  [15:0] A,
  input  [15:0] B,
  input  [1:0] aluMux,
  input  aluMuxEnb,
  output [15:0] outALU,
  output A_greaterB,
  output A_equalB,
  output A_lessB
);

  wire [15:0] adder_1_out, divider_1_out, multiplier_1_out, subtractor_1_out;

  Adder #(.width(16)) adder_1 (.a(A), .b(B), .out(adder_1_out));  // open: cin, cout
  Subtractor #(.width(16)) subtractor_1 (.a(A), .b(B), .out(subtractor_1_out));  // open: bin, bout
  Multiplier #(.width(16)) multiplier_1 (.a(A), .b(B), .out(multiplier_1_out));  // open: cin, cout
  Divider #(.width(16)) divider_1 (.a(A), .b(B), .out(divider_1_out));  // open: upper, rem
  Comparator #(.mode("unsigned"), .width(16)) comparator_1 (.a(A), .b(B), .gt(A_greaterB), .eq(A_equalB), .lt(A_lessB));
  Multiplexer #(.enable("true"), .select(2), .width(16)) multiplexer_1 (
    .in0(adder_1_out), .in1(subtractor_1_out), .in2(multiplier_1_out), .in3(divider_1_out), .out(outALU),
    .sel(aluMux), .en(aluMuxEnb));
endmodule

module regFile (
  input  CLK,
  input  [15:0] regData,
  input  WE,
  input  [1:0] regSelect,
  input  [1:0] outRegSel,
  output [15:0] regOut,
  output [15:0] r0,
  output [15:0] r1,
  output [15:0] r2,
  output [15:0] r3
);

  wire demultiplexer_1_out0, demultiplexer_1_out1, demultiplexer_1_out2, demultiplexer_1_out3;

  Demultiplexer #(.select(2)) demultiplexer_1 (
    .out0(demultiplexer_1_out0), .out1(demultiplexer_1_out1), .out2(demultiplexer_1_out2),
    .out3(demultiplexer_1_out3), .in(WE), .sel(regSelect));
  Register #(.width(16)) register_1 (.D(regData), .en(demultiplexer_1_out0), .clk(CLK), .Q(r0));  // open: clr
  Register #(.width(16)) register_2 (.D(regData), .en(demultiplexer_1_out1), .clk(CLK), .Q(r1));  // open: clr
  Register #(.width(16)) register_3 (.D(regData), .en(demultiplexer_1_out2), .clk(CLK), .Q(r2));  // open: clr
  Register #(.width(16)) register_4 (.D(regData), .en(demultiplexer_1_out3), .clk(CLK), .Q(r3));  // open: clr
  Multiplexer #(.select(2), .width(16)) multiplexer_1 (
    .in0(r0), .in1(r1), .in2(r2), .in3(r3), .out(regOut), .sel(outRegSel));
endmodule

module controlUnit (
  input  CLK,
  input  [27:0] Instruction,
  output [9:0] out_3
);

  wire and_1_out, comparator_1_eq, not_1_out, register_1_q;
  wire [4:0] counter_1_q;

  Comparator #(.width(28)) comparator_1 (.a(Instruction), .b(28'h1), .eq(comparator_1_eq));  // open: gt, lt
  Register #(.width(1)) register_1 (.D(comparator_1_eq), .en(not_1_out), .clk(CLK), .Q(register_1_q), .clr(and_1_out));
  not not_1 (not_1_out, register_1_q);
  Counter #(.max('h1f), .width(5)) counter_1 (
    .count(register_1_q), .Q(counter_1_q), .clk(CLK), .clr(and_1_out));  // open: load, D, carry, up
  ROM #(.addrWidth(5), .dataWidth(10)) rom_1 (.addr(counter_1_q), .data(out_3));
  and and_1 (and_1_out, out_3[9], out_3[8]);

  // Notes on the sheet:
  //   contents of rom_1 (hex, n*v repeats v):
  //   26*0 3ff
endmodule
