// Logisim project t4_slopeCalc_unsigned.circ as structural Verilog: 1 circuit, main circuit main
module main (
  input  in_1,
  input  [7:0] x0,
  input  [7:0] x1,
  input  [7:0] y0,
  input  [7:0] y1,
  output [7:0] out_6
);

  wire decoder_1_out0, decoder_1_out1, decoder_1_out2;
  wire [1:0] counter_1_q;
  wire [7:0] deltaX_q, deltaY_q, divider_1_out, random_1_out, random_2_out, random_3_out, random_4_out,
       subtractor_1_out, subtractor_2_out;

  Random random_1 (.clk(in_1), .out(random_1_out));  // open: clr, next
  Random #(.seed(4)) random_2 (.clk(in_1), .out(random_2_out));  // open: clr, next
  Random #(.seed(5)) random_3 (.clk(in_1), .out(random_3_out));  // open: clr, next
  Random random_4 (.clk(in_1), .out(random_4_out));  // open: clr, next
  Subtractor subtractor_1 (.a(random_1_out), .b(random_2_out), .out(subtractor_1_out));  // open: bin, bout
  Subtractor subtractor_2 (.a(random_3_out), .b(random_4_out), .out(subtractor_2_out));  // open: bin, bout
  Counter #(.max('h3), .width(2)) counter_1 (
    .Q(counter_1_q), .clk(in_1), .clr(decoder_1_out2));  // open: load, D, count, carry, up
  Decoder #(.select(2)) decoder_1 (
    .out0(decoder_1_out0), .out1(decoder_1_out1), .out2(decoder_1_out2), .sel(counter_1_q));  // open: out3, en
  Register deltaX (.D(subtractor_1_out), .en(decoder_1_out0), .clk(in_1), .Q(deltaX_q));  // open: clr
  Register deltaY (.D(subtractor_2_out), .en(decoder_1_out0), .clk(in_1), .Q(deltaY_q));  // open: clr
  Divider divider_1 (.a(deltaX_q), .b(deltaY_q), .out(divider_1_out));  // open: upper, rem
  Register dy_dx (.D(divider_1_out), .en(decoder_1_out1), .clk(in_1), .Q(out_6));  // open: clr
endmodule
